// Digital circuit TBOS Testing.dig as structural Verilog
module TBOS_Testing (
  input  clk
);

  wire button_1_out, button_2_out, button_3_out, telescope_computing_system_1_running;
  wire [15:0] Root_Drive_d, TBOS_2_1_d, telescope_computing_system_1_os_adr,
       telescope_computing_system_1_status_code;
  wire [18:0] telescope_computing_system_1_tk1_out;
  wire [33:0] telescope_computing_system_1_d0_out;

  LED OS_Is_Running (.in(telescope_computing_system_1_running));
  // Probe Status on telescope_computing_system_1_status_code
  Button button_1 (.out(button_1_out));
  Telescope_Computing_System telescope_computing_system_1 (
    .Running(telescope_computing_system_1_running), .Status_Code(telescope_computing_system_1_status_code),
    .Power_On(button_1_out), .Clock_Input(clk), .Pause_CPU(button_2_out), .PAUS(1'b0), .STOP(button_3_out),
    .OS_Adr(telescope_computing_system_1_os_adr), .OS_In(TBOS_2_1_d), .D0_In(Root_Drive_d),
    .D0_Out(telescope_computing_system_1_d0_out), .D1_In({16{1'b0}}), .D2_In({16{1'b0}}), .D3_In({16{1'b0}}),
    .TNET_I_0({20{1'b0}}), .TNET_I_1({20{1'b0}}), .TNET_I_2({20{1'b0}}), .TNET_I_3({20{1'b0}}),
    .K0_In({17{1'b0}}), .TK1_Out(telescope_computing_system_1_tk1_out), .K1_In({17{1'b0}}),
    .K2_In({17{1'b0}}), .K3_In({17{1'b0}}), .GPI_0({18{1'b0}}), .GPI_1({18{1'b0}}), .GPI_2({18{1'b0}}),
    .GPI_3({18{1'b0}}));  // open: D1_Out, D2_Out, D3_Out, TNET_O_0, TNET_O_1, TNET_O_2, TNET_O_3, TK0_Out, TK2_Out, TK3_Out, GPO_0, GPO_1, GPO_2, GPO_3
  Button button_2 (.out(button_2_out));
  Button button_3 (.out(button_3_out));
  // Probe OS Boot Address on telescope_computing_system_1_os_adr
  ROM #(.AddrBits(16), .Bits(16)) TBOS_2_1 (.A(telescope_computing_system_1_os_adr), .sel(1'b1), .D(TBOS_2_1_d));
  Terminal terminal_1 (
    .D(telescope_computing_system_1_tk1_out[15:0]), .C(telescope_computing_system_1_tk1_out[18]),
    .en(telescope_computing_system_1_tk1_out[17]));
  EEPROMDualPort #(.AddrBits(16), .Bits(16)) Root_Drive (
    .A(telescope_computing_system_1_d0_out[15:0]), .Din(telescope_computing_system_1_d0_out[31:16]),
    .str(telescope_computing_system_1_d0_out[32]), .C(telescope_computing_system_1_d0_out[33]), .ld(1'b1),
    .D(Root_Drive_d));

  // Notes on the sheet:
  //   clk: Hz: 4096
  //   contents of TBOS_2_1 (hex, n*v repeats v):
  //   786,4600,22e,520*0,32*1,0,0,a654,a754,5000,1,50a0,f000,3090,50a0
  //   ,e000,3090,5010,786,5000,400,ae10,b912,5000,40,bb01,3078,b974
  //   ,4600,367,50a0,0,3078,b974,4600,5d4,d961,4a00,250,5000,ff00,4600
  //   ,261,3006,50a0,4,3078,b974,4600,390,5000,2,50a0,f000,3090,b000
  //   ,7000,64,4600,26a,50a0,e800,3090,50a0,f000,3090,0,4600,267,b100
  //   ,6000,62,9200,4000,2b0,b100,6000,64,3060,b110,6011,63,b911,b150
  //   ,af61,b901,af01,cb06,4800,283,b951,db56,4000,2b4,6020,66,d620
  //   ,4a00,27a,d622,4200,27a,7000,64,bd0c,5010,86,a901,7000,65,60e0
  //   ,a,50f0,2be,50d0,200,60c0,b,60a0,8,60b0,9,6070,7,6060,6,6050,5
  //   ,6040,4,6030,3,6020,2,6010,1,6000,0,1000,5000,600d,4600,261,b100
  //   ,6000,22b,9200,4800,67c,5000,dead,4600,261,7000,306,b100,6000
  //   ,65,7010,1,b110,6011,306,7010,0,7020,2,7030,3,7040,4,7050,5,7060
  //   ,6,7070,7,70b0,9,70e0,a,70a0,8,b1b0,5000,700,a10a,b508,db04,4000
  //   ,26a,db05,4000,691,db06,4000,645,db07,4000,645,db01,4000,448,db03
  //   ,4000,44f,db00,4000,45b,db02,4800,302,b100,6000,65,5010,ff03,7010
  //   ,6,4600,26a,5000,ff01,4600,261,0,b100,6000,64,6000,66,d602,4200
  //   ,26a,b100,6000,65,60b0,9,60a0,8,6070,7,6060,6,6050,5,6040,4,6030
  //   ,3,6020,2,6010,1,6000,0,1000,9210,4000,330,7090,0,b901,9b11,4800
  //   ,32a,3087,b110,6031,206,5040,10,3051,af54,c635,4200,354,5020,1
  //   ,3051,a952,cb20,4000,363,cf54,4800,34a,3065,ae64,bf64,6036,206
  //   ,3065,af64,c636,4200,353,b951,b921,4600,33f,3015,b911,5050,40
  //   ,cb51,4100,365,cf14,4800,336,3051,ae54,6035,206,4600,336,3061
  //   ,3087,b060,3087,b120,6022,22c,7022,37d,4600,375,b120,6022,22d
  //   ,7022,37d,4600,375,5020,10,3030,ae32,6053,206,3040,af42,f000,b941
  //   ,9b11,4000,38d,8f42,4800,37d,7053,206,b931,bf34,6053,206,4600
  //   ,37d,7053,206,3087,bbb1,70ab,0,b010,b911,3021,bd23,6032,2,d63f
  //   ,4200,394,b130,b63f,7032,2,b130,b921,7032,2,b921,7032,2,6033,62
  //   ,b931,7033,62,b140,6044,63,cb14,4100,3b4,7011,63,5040,1,7041,66
  //   ,3021,bd2c,5030,86,a923,b130,7032,0,7032,1,7032,2,7032,3,7032
  //   ,4,7032,5,7032,6,7032,7,7032,a,7032,9,603b,0,7032,8,7002,b,3001
  //   ,3060,b9b1,4600,3dd,9200,4000,411,3010,bd13,6021,2,5030,3e0,a033
  //   ,a123,5030,7c00,a033,a123,b130,6033,64,3043,b44a,a224,7021,2,bd33
  //   ,6023,2,5010,1f,8112,4800,400,a220,7023,2,3087,bd13,6021,2,5030
  //   ,3e0,8132,4000,40c,b535,3013,4600,400,3030,b435,a223,7021,2,3087
  //   ,9200,4000,447,3050,bd53,6055,2,5020,7c00,a125,b52a,bd23,6032
  //   ,2,5040,1f,a143,cb40,4800,432,5040,1f,a044,a134,5040,3e0,a145
  //   ,b545,a234,7032,2,3087,bd43,6024,2,5030,3e0,a132,b535,cb30,4000
  //   ,43f,3043,4600,432,5030,3e0,a153,a033,a123,a225,7024,2,3087,50a0
  //   ,f000,5090,1000,0,4600,307,50a0,f000,5090,2222,0,b100,3078,b974
  //   ,4600,466,4600,26a,5000,22a,3078,b974,4600,585,50a0,f800,b190
  //   ,4600,307,bbb1,707b,0,b110,3078,b974,4600,482,b100,6000,63,9200
  //   ,4000,47c,6010,66,d610,4200,47c,bb01,4600,471,7000,63,607b,0,b9b1
  //   ,3087,bbb3,700b,0,707b,1,3020,bd23,6022,2,702b,2,9210,4000,49b
  //   ,5030,3e0,8123,4000,49f,b525,3002,5070,49f,4600,482,3078,b974
  //   ,4600,412,600b,0,6030,66,d632,4a00,4df,3010,bd13,b911,6021,2,d633
  //   ,4a00,4b4,b130,6033,22b,bb31,7033,22b,3041,b911,6011,2,b130,7034
  //   ,2,b941,7034,2,6032,0,b931,7032,0,b030,b160,6066,63,b961,b931
  //   ,cb36,4000,4df,3043,bd43,b941,6054,2,cb52,4800,4c8,b941,6054,2
  //   ,cb51,4900,4c8,b951,7054,2,4600,4c8,6010,66,d611,4200,4fb,3020
  //   ,bd2c,b92b,6022,86,9200,4000,4ec,3012,5030,400,ae13,5000,ff,a102
  //   ,b408,ae03,3078,b974,4600,36e,600b,0,602b,2,5030,1f,8123,4000
  //   ,50a,3002,b010,3078,b974,4600,482,600b,0,3020,bd23,b110,7012,2
  //   ,b110,6011,62,bb11,7011,62,b110,7010,66,607b,1,b9b3,3087,6020
  //   ,0,bb21,7020,0,9220,4900,545,3031,bd33,b931,7003,2,b931,7023,2
  //   ,6031,66,b632,5020,22a,cb02,4100,540,5020,22b,cb02,4900,540,b120
  //   ,6022,22b,b921,7022,22b,b633,7031,66,5060,1,3087,b160,3087,6010
  //   ,0,b911,7010,0,b010,b120,6022,63,b921,b911,cb12,4000,584,3031
  //   ,bd33,b931,6043,2,cb40,4800,551,b931,6043,2,b941,7043,2,9240,4100
  //   ,551,b140,7043,2,bb31,7043,2,6031,66,b732,5040,22a,cb04,4100,580
  //   ,5040,22b,cb04,4900,580,b140,6044,22b,bb41,7044,22b,b733,7031
  //   ,66,4600,551,3087,b010,b120,b911,5030,20,cb13,4000,5b4,3031,bd33
  //   ,b931,6043,2,cb40,4800,587,6061,66,b762,5050,22a,cb45,4100,5a9
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  //   contents of Root_Drive (hex, n*v repeats v):
  //   e8,4600,26,4*0,6*41,ffff,6*42,ffff,6*43,ffff,a,41,6c,6c,20,64
  //   ,6f,6e,65,21,ffff,5000,1,5020,e8,b130,5010,46,2000,5010,7a,2000
  //   ,5010,9f,2000,5000,4,5010,5,2000,5000,5,5010,2,2000,5000,4,5010
  //   ,5,2000,5000,2,2000,5000,6,3078,b974,4600,b8,5000,4,5010,3,2000,2000
  //   ,5000,1,5010,b3,5020,e8,b130,2000,5000,3,2000,b110,6011,2,d911
  //   ,4800,5c,5000,5,5010,4,2000,5000,3,2000,b110,6011,2,d912,4800
  //   ,6a,5020,2,5000,5,5010,5,2000,3002,2000,5000,8,2000,5000,d,3078
  //   ,b974,4600,b8,5000,5,5010,3,2000,5000,4,5010,4,2000,2000,5010
  //   ,2,2000,5000,1b,3078,b974,4600,b8,5000,5,5010,5,2000,5000,2,2000
  //   ,5000,8,2000,5000,14,3078,b974,4600,b8,5000,5,5010,3,2000,5010
  //   ,4,2000,5000,2,2000,5000,4,5010,2,2000,3010,5000,3,50a0,4800,6021
  //   ,0,3092,2000,b911,6021,0,d921,4a00,bf,3087
  //   Currently running: Small Threading Test
endmodule
